// Logisim project CPU-SC.circ as structural Verilog: 6 circuits, main circuit main
module main (
);

  wire control_unit_1_out_3, control_unit_1_out_4, control_unit_1_out_5, control_unit_1_out_6,
       control_unit_1_out_7, control_unit_1_out_8, control_unit_1_out_9, control_unit_1_out_10, or_1_out,
       reloj_1_out_1, reloj_1_out_2, reloj_1_out_3, reloj_1_out_4, reloj_1_out_5;
  wire [3:0] control_unit_1_out_2;
  wire [4:0] multiplexer_1_out;
  wire [27:0] register_1_q;
  wire [31:0] adder_1_out, adder_2_out, alu_1_a_2, bit_extender_1_out, data_memory_1_out_6,
       multiplexer_2_out, multiplexer_3_out, multiplexer_4_out, multiplexer_5_out, PC_q, register_3_q,
       register_4_q, register_5_q, register_6_q, register_7_q, register_8_q, register_9_q, register_10_q,
       registerfile_1_rd1, registerfile_1_rd2, rom_1_data, shifter_1_out;
  wire [31:2] register_2_q_2;
  wire [31:26] register_2_q;

  Register #(.width(32), .Select("low")) PC (.D(multiplexer_3_out), .Q(PC_q), .clk(reloj_1_out_1));  // open: en, clr
  Adder #(.width(32)) adder_1 (.a(32'h4), .b(PC_q), .out(adder_1_out));  // open: cin, cout
  ROM #(.dataWidth(32), .Select("low")) rom_1 (.addr(PC_q[9:2]), .data(rom_1_data));
  Register #(.width(32), .Select("low")) register_1 (
    .D(adder_1_out), .Q({register_2_q_2[31:28], register_1_q}), .clk(reloj_1_out_2));  // open: en, clr
  Register #(.width(32), .Select("low")) register_2 (
    .D(rom_1_data), .Q({register_2_q, register_2_q_2[27:2]}), .clk(reloj_1_out_2));  // open: en, clr
  Reloj reloj_1 (
    .out_1(reloj_1_out_1), .out_2(reloj_1_out_2), .out_3(reloj_1_out_3), .out_4(reloj_1_out_4),
    .out_5(reloj_1_out_5));
  Control_Unit control_unit_1 (
    .in_1({register_2_q, register_2_q_2[27:2]}), .out_2(control_unit_1_out_2), .out_3(control_unit_1_out_3),
    .out_4(control_unit_1_out_4), .out_5(control_unit_1_out_5), .out_6(control_unit_1_out_6),
    .out_7(control_unit_1_out_7), .out_8(control_unit_1_out_8), .out_9(control_unit_1_out_9),
    .out_10(control_unit_1_out_10));
  Multiplexer #(.width(5), .enable("false")) multiplexer_1 (
    .in0(register_2_q_2[22:18]), .in1(register_2_q_2[17:13]), .out(multiplexer_1_out),
    .sel(control_unit_1_out_9));
  assign bit_extender_1_out = {{16{register_2_q[31]}}, {register_2_q, register_2_q_2[27:18]}};  // Bit_Extender bit_extender_1
  or or_1 (or_1_out, reloj_1_out_2, reloj_1_out_5);
  Shifter #(.width(32)) shifter_1 (.in(bit_extender_1_out), .\dist (5'b00010), .out(shifter_1_out));
  Register #(.width(32), .Select("low")) register_3 (
    .D({register_2_q_2[31:28], register_1_q}), .Q(register_3_q), .clk(reloj_1_out_3));  // open: en, clr
  Register #(.width(32), .Select("low")) register_4 (
    .D(registerfile_1_rd1), .Q(register_4_q), .clk(reloj_1_out_3));  // open: en, clr
  RegisterFile registerfile_1 (
    .rs(register_2_q_2[27:23]), .rt(register_2_q_2[22:18]), .rd(multiplexer_1_out),
    .WriteData(register_10_q), .RegWrite(control_unit_1_out_10), .rd1(registerfile_1_rd1),
    .rd2(registerfile_1_rd2), .Clock(or_1_out));
  Register #(.width(32), .Select("low")) register_5 (
    .D(registerfile_1_rd2), .Q(register_5_q), .clk(reloj_1_out_3));  // open: en, clr
  Register #(.width(32), .Select("low")) register_6 (
    .D(registerfile_1_rd2), .Q(register_6_q), .clk(reloj_1_out_3));  // open: en, clr
  Multiplexer #(.width(32), .enable("false")) multiplexer_2 (
    .in0(register_5_q), .in1(bit_extender_1_out), .out(multiplexer_2_out), .sel(control_unit_1_out_3));
  ALU alu_1 (
    .AluOP(control_unit_1_out_2), .A(register_4_q), .B(multiplexer_2_out), .in_4(reloj_1_out_3),
    .A_2(alu_1_a_2));  // open: out_6
  Adder #(.width(32)) adder_2 (.a(shifter_1_out), .b(register_3_q), .out(adder_2_out));  // open: cin, cout
  Register #(.width(32), .Select("low")) register_7 (
    .D(register_3_q), .Q(register_7_q), .clk(reloj_1_out_4));  // open: en, clr
  Register #(.width(32), .Select("low")) register_8 (
    .D(alu_1_a_2), .Q(register_8_q), .clk(reloj_1_out_4));  // open: en, clr
  Register #(.width(32), .Select("low")) register_9 (
    .D(register_6_q), .Q(register_9_q), .clk(reloj_1_out_4));  // open: en, clr
  Multiplexer #(.width(32), .enable("false")) multiplexer_3 (
    .in0(multiplexer_4_out), .in1({register_2_q_2, 2'b00}), .out(multiplexer_3_out),
    .sel(control_unit_1_out_4));
  Multiplexer #(.width(32), .enable("false")) multiplexer_4 (
    .in0(register_7_q), .in1(adder_2_out), .out(multiplexer_4_out), .sel(control_unit_1_out_8));
  Data_Memory data_memory_1 (
    .BMemRead(control_unit_1_out_5), .Address(register_8_q), .BMemWrite(control_unit_1_out_6),
    .WriteData(register_9_q), .in_5(reloj_1_out_4), .out_6(data_memory_1_out_6));
  Multiplexer #(.width(32), .enable("false")) multiplexer_5 (
    .in0(register_8_q), .in1(data_memory_1_out_6), .out(multiplexer_5_out), .sel(control_unit_1_out_7));
  Register #(.width(32), .Select("low")) register_10 (
    .D(multiplexer_5_out), .Q(register_10_q), .clk(reloj_1_out_5));  // open: en, clr

  // Notes on the sheet:
  //   contents of rom_1 (hex, n*v repeats v):
  //   ac420000
endmodule

module RegisterFile (
  input  Clock,
  input  [4:0] rs,
  input  [4:0] rt,
  input  [4:0] rd,
  input  [31:0] WriteData,
  input  RegWrite,
  output [31:0] rd1,
  output [31:0] rd2
);

  wire demultiplexer_1_out1, demultiplexer_1_out2, demultiplexer_1_out3, demultiplexer_1_out4,
       demultiplexer_1_out5, demultiplexer_1_out6, demultiplexer_1_out7, demultiplexer_1_out8,
       demultiplexer_1_out9, demultiplexer_1_out10, demultiplexer_1_out11, demultiplexer_1_out12,
       demultiplexer_1_out13, demultiplexer_1_out14, demultiplexer_1_out15, demultiplexer_1_out16,
       demultiplexer_1_out17, demultiplexer_1_out18, demultiplexer_1_out19, demultiplexer_1_out20,
       demultiplexer_1_out21, demultiplexer_1_out22, demultiplexer_1_out23, demultiplexer_1_out24,
       demultiplexer_1_out25, demultiplexer_1_out26, demultiplexer_1_out27, demultiplexer_1_out28,
       demultiplexer_1_out29, demultiplexer_1_out30, demultiplexer_1_out31, undriven;
  wire [31:0] r1_q, r2_q, r3_q, r4_q, r5_q, r6_q, r7_q, r8_q, r9_q, r10_q, r11_q, r12_q, r13_q, r14_q, r15_q,
       r16_q, r17_q, r18_q, r19_q, r20_q, r21_q, r22_q, r23_q, r24_q, r25_q, r26_q, r27_q, r28_q, r29_q,
       r30_q, r31_q;

  Demultiplexer #(.select(5), .enable("false")) demultiplexer_1 (
    .out1(demultiplexer_1_out1), .out2(demultiplexer_1_out2), .out3(demultiplexer_1_out3),
    .out4(demultiplexer_1_out4), .out5(demultiplexer_1_out5), .out6(demultiplexer_1_out6),
    .out7(demultiplexer_1_out7), .out8(demultiplexer_1_out8), .out9(demultiplexer_1_out9),
    .out10(demultiplexer_1_out10), .out11(demultiplexer_1_out11), .out12(demultiplexer_1_out12),
    .out13(demultiplexer_1_out13), .out14(demultiplexer_1_out14), .out15(demultiplexer_1_out15),
    .out16(demultiplexer_1_out16), .out17(demultiplexer_1_out17), .out18(demultiplexer_1_out18),
    .out19(demultiplexer_1_out19), .out20(demultiplexer_1_out20), .out21(demultiplexer_1_out21),
    .out22(demultiplexer_1_out22), .out23(demultiplexer_1_out23), .out24(demultiplexer_1_out24),
    .out25(demultiplexer_1_out25), .out26(demultiplexer_1_out26), .out27(demultiplexer_1_out27),
    .out28(demultiplexer_1_out28), .out29(demultiplexer_1_out29), .out30(demultiplexer_1_out30),
    .out31(demultiplexer_1_out31), .in(RegWrite), .sel(rd));  // open: out0
  Register #(.width(32), .Select("low")) r16 (
    .D(WriteData), .en(demultiplexer_1_out16), .Q(r16_q), .clk(Clock));  // open: clr
  Register #(.width(32), .Select("low")) r24 (
    .D(WriteData), .en(demultiplexer_1_out24), .Q(r24_q), .clk(Clock));  // open: clr
  Register #(.width(32), .Select("low")) r1 (
    .D(WriteData), .en(demultiplexer_1_out1), .Q(r1_q), .clk(Clock));  // open: clr
  Register #(.width(32), .Select("low")) r8 (
    .D(WriteData), .en(demultiplexer_1_out8), .Q(r8_q), .clk(Clock));  // open: clr
  Register #(.width(32), .Select("low")) r17 (
    .D(WriteData), .en(demultiplexer_1_out17), .Q(r17_q), .clk(Clock));  // open: clr
  Register #(.width(32), .Select("low")) r25 (
    .D(WriteData), .en(demultiplexer_1_out25), .Q(r25_q), .clk(Clock));  // open: clr
  Register #(.width(32), .Select("low")) r2 (
    .D(WriteData), .en(demultiplexer_1_out2), .Q(r2_q), .clk(Clock));  // open: clr
  Register #(.width(32), .Select("low")) r9 (
    .D(WriteData), .en(demultiplexer_1_out9), .Q(r9_q), .clk(Clock));  // open: clr
  Register #(.width(32), .Select("low")) r18 (
    .D(WriteData), .en(demultiplexer_1_out18), .Q(r18_q), .clk(Clock));  // open: clr
  Register #(.width(32), .Select("low")) r26 (
    .D(WriteData), .en(demultiplexer_1_out26), .Q(r26_q), .clk(Clock));  // open: clr
  Register #(.width(32), .Select("low")) r3 (
    .D(WriteData), .en(demultiplexer_1_out3), .Q(r3_q), .clk(Clock));  // open: clr
  Register #(.width(32), .Select("low")) r10 (
    .D(WriteData), .en(demultiplexer_1_out10), .Q(r10_q), .clk(Clock));  // open: clr
  Register #(.width(32), .Select("low")) r19 (
    .D(WriteData), .en(demultiplexer_1_out19), .Q(r19_q), .clk(Clock));  // open: clr
  Register #(.width(32), .Select("low")) r27 (
    .D(WriteData), .en(demultiplexer_1_out27), .Q(r27_q), .clk(Clock));  // open: clr
  Register #(.width(32), .Select("low")) r4 (
    .D(WriteData), .en(demultiplexer_1_out4), .Q(r4_q), .clk(Clock));  // open: clr
  Register #(.width(32), .Select("low")) r11 (
    .D(WriteData), .en(demultiplexer_1_out11), .Q(r11_q), .clk(Clock));  // open: clr
  Register #(.width(32), .Select("low")) r20 (
    .D(WriteData), .en(demultiplexer_1_out20), .Q(r20_q), .clk(Clock));  // open: clr
  Register #(.width(32), .Select("low")) r28 (
    .D(WriteData), .en(demultiplexer_1_out28), .Q(r28_q), .clk(Clock));  // open: clr
  Register #(.width(32), .Select("low")) r5 (
    .D(WriteData), .en(demultiplexer_1_out5), .Q(r5_q), .clk(Clock));  // open: clr
  Register #(.width(32), .Select("low")) r12 (
    .D(WriteData), .en(demultiplexer_1_out12), .Q(r12_q), .clk(Clock));  // open: clr
  Register #(.width(32), .Select("low")) r21 (
    .D(WriteData), .en(demultiplexer_1_out21), .Q(r21_q), .clk(Clock));  // open: clr
  Register #(.width(32), .Select("low")) r29 (
    .D(WriteData), .en(demultiplexer_1_out29), .Q(r29_q), .clk(Clock));  // open: clr
  Register #(.width(32), .Select("low")) r6 (
    .D(WriteData), .en(demultiplexer_1_out6), .Q(r6_q), .clk(Clock));  // open: clr
  Register #(.width(32), .Select("low")) r13 (
    .D(WriteData), .en(demultiplexer_1_out13), .Q(r13_q), .clk(Clock));  // open: clr
  Register #(.width(32), .Select("low")) r30 (
    .D(WriteData), .en(demultiplexer_1_out30), .Q(r30_q), .clk(Clock), .clr(undriven));
  Register #(.width(32), .Select("low")) r7 (
    .D(WriteData), .en(demultiplexer_1_out7), .Q(r7_q), .clk(Clock));  // open: clr
  Register #(.width(32), .Select("low")) r14 (
    .D(WriteData), .en(demultiplexer_1_out14), .Q(r14_q), .clk(Clock));  // open: clr
  Register #(.width(32), .Select("low")) r22 (
    .D(WriteData), .en(demultiplexer_1_out22), .Q(r22_q), .clk(Clock));  // open: clr
  Register #(.width(32), .Select("low")) r23 (
    .D(WriteData), .en(demultiplexer_1_out23), .Q(r23_q), .clk(Clock));  // open: clr
  Register #(.width(32), .Select("low")) r31 (
    .D(WriteData), .en(demultiplexer_1_out31), .Q(r31_q), .clk(Clock));  // open: clr
  Register #(.width(32), .Select("low")) r15 (
    .D(WriteData), .en(demultiplexer_1_out15), .Q(r15_q), .clk(Clock));  // open: clr
  Multiplexer #(.select(5), .width(32), .enable("false")) multiplexer_1 (
    .in0({32{1'b0}}), .in1(r1_q), .in2(r2_q), .in3(r3_q), .in4(r4_q), .in5(r5_q), .in6(r6_q), .in7(r7_q),
    .in8(r8_q), .in9(r9_q), .in10(r10_q), .in11(r11_q), .in12(r12_q), .in13(r13_q), .in14(r14_q),
    .in15(r15_q), .in16(r16_q), .in17(r17_q), .in18(r18_q), .in19(r19_q), .in20(r20_q), .in21(r21_q),
    .in22(r22_q), .in23(r23_q), .in24(r24_q), .in25(r25_q), .in26(r26_q), .in27(r27_q), .in28(r28_q),
    .in29(r29_q), .in30(r30_q), .in31(r31_q), .out(rd1), .sel(rs));
  Multiplexer #(.select(5), .width(32), .enable("false")) multiplexer_2 (
    .in0({32{1'b0}}), .in1(r1_q), .in2(r2_q), .in3(r3_q), .in4(r4_q), .in5(r5_q), .in6(r6_q), .in7(r7_q),
    .in8(r8_q), .in9(r9_q), .in10(r10_q), .in11(r11_q), .in12(r12_q), .in13(r13_q), .in14(r14_q),
    .in15(r15_q), .in16(r16_q), .in17(r17_q), .in18(r18_q), .in19(r19_q), .in20(r20_q), .in21(r21_q),
    .in22(r22_q), .in23(r23_q), .in24(r24_q), .in25(r25_q), .in26(r26_q), .in27(r27_q), .in28(r28_q),
    .in29(r29_q), .in30(r30_q), .in31(r31_q), .out(rd2), .sel(rt));

  // Notes on the sheet:
  //   Register File
  //   Entradas
  //   Datapath
  //   Control
  //   Salidas
endmodule

module Reloj (
  output out_1,
  output out_2,
  output out_3,
  output out_4,
  output out_5
);

  wire clock_1_out;
  wire [2:0] counter_1_q;

  Counter #(.width(3), .max('h5)) counter_1 (
    .Q(counter_1_q), .clk(clock_1_out));  // open: load, D, count, carry, clr, preset, down
  Clock clock_1 (.out(clock_1_out));
  ROM #(.addrWidth(3), .dataWidth(5), .Select("low")) rom_1 (
    .addr(counter_1_q), .data({out_5, out_4, out_3, out_2, out_1}));

  // Other names for the same wires on the sheet: _1 = out_1; _2 = out_2; _3 = out_3; _4 = out_4; _5 = out_5

  // Notes on the sheet:
  //   contents of rom_1 (hex, n*v repeats v):
  //   0 1 2 4 8 10
endmodule

module ALU (
  input  [3:0] AluOP,
  input  [31:0] A,
  input  [31:0] B,
  input  in_4,
  output [31:0] A_2,
  output out_6
);

  wire comparator_1_gt, comparator_2_gt;
  wire [4:0] bit_extender_1_out, bit_extender_2_out, bit_extender_3_out;
  wire [31:0] adder_1_out, and_1_out, divider_1_out, multiplexer_1_out, multiplexer_2_out, multiplier_1_out,
       nand_1_out, negator_1_out, nor_1_out, not_1_out, or_1_out, shifter_1_out, shifter_2_out,
       shifter_3_out, subtractor_1_out, subtractor_2_out, subtractor_3_out, xor_1_out;

  Adder #(.width(32)) adder_1 (.a(A), .b(B), .out(adder_1_out));  // open: cin, cout
  Subtractor #(.width(32)) subtractor_1 (.a(A), .b(B), .out(subtractor_1_out));  // open: bin, bout
  Multiplier #(.width(32)) multiplier_1 (.a(A), .b(B), .out(multiplier_1_out));  // open: cin, cout
  Divider #(.width(32)) divider_1 (.a(A), .b(B), .out(divider_1_out));  // open: upper, rem
  assign and_1_out = A & B;  // AND_Gate and_1, 32 bits wide
  assign or_1_out = A | B;  // OR_Gate or_1, 32 bits wide
  assign xor_1_out = A ^ B;  // XOR_Gate xor_1, 32 bits wide
  assign not_1_out = ~A;  // NOT_Gate not_1, 32 bits wide
  assign nand_1_out = ~(A & B);  // NAND_Gate nand_1, 32 bits wide
  assign nor_1_out = ~(A | B);  // NOR_Gate nor_1, 32 bits wide
  Subtractor #(.width(32)) subtractor_2 (.a(A), .b(B), .out(subtractor_2_out));  // open: bin, bout
  Subtractor #(.width(32)) subtractor_3 (.a(A), .b(B), .out(subtractor_3_out));  // open: bin, bout
  Bit_Extender #(.in_width(32), .out_width(5), .\type ("zero")) bit_extender_1 (.in(B), .out(bit_extender_1_out));
  Bit_Extender #(.in_width(32), .out_width(5), .\type ("zero")) bit_extender_2 (.in(B), .out(bit_extender_2_out));
  Bit_Extender #(.in_width(32), .out_width(5), .\type ("zero")) bit_extender_3 (.in(B), .out(bit_extender_3_out));
  Shifter #(.width(32)) shifter_1 (.in(A), .\dist (bit_extender_1_out), .out(shifter_1_out));
  Shifter #(.width(32), .shift("lr")) shifter_2 (.in(A), .\dist (bit_extender_2_out), .out(shifter_2_out));
  Shifter #(.width(32), .shift("ar")) shifter_3 (.in(A), .\dist (bit_extender_3_out), .out(shifter_3_out));
  Negator #(.width(32)) negator_1 (.in(A), .out(negator_1_out));
  Comparator #(.width(32)) comparator_1 (
    .a(subtractor_2_out), .b({32{1'b0}}), .gt(comparator_1_gt), .eq(out_6));  // open: lt
  Comparator #(.width(32), .mode("unsigned")) comparator_2 (
    .a(subtractor_3_out), .b({32{1'b0}}), .gt(comparator_2_gt));  // open: eq, lt
  Multiplexer #(.width(32), .enable("false")) multiplexer_1 (
    .in0({32{1'b0}}), .in1(32'h1), .out(multiplexer_1_out), .sel(comparator_1_gt));
  Multiplexer #(.width(32), .enable("false")) multiplexer_2 (
    .in0({32{1'b0}}), .in1(32'h1), .out(multiplexer_2_out), .sel(comparator_2_gt));
  Multiplexer #(.select(4), .width(32), .enable("false")) multiplexer_3 (
    .in0(adder_1_out), .in1(subtractor_1_out), .in2(multiplier_1_out), .in3(divider_1_out), .in4(and_1_out),
    .in5(or_1_out), .in6(xor_1_out), .in7(not_1_out), .in8(nand_1_out), .in9(nor_1_out),
    .in10(multiplexer_1_out), .in11(multiplexer_2_out), .in12(shifter_1_out), .in13(shifter_2_out),
    .in14(shifter_3_out), .in15(negator_1_out), .out(A_2), .sel(AluOP));

  // Other names for the same wires on the sheet: Clock = in_4; Result[31:0] = A_2; Zero = out_6

  // Notes on the sheet:
  //   ALU
  //   Operand 1
  //   Operand 2
endmodule

module Control_Unit (
  input  [31:0] in_1,
  output [3:0] out_2,
  output out_3,
  output out_4,
  output out_5,
  output out_6,
  output out_7,
  output out_8,
  output out_9,
  output out_10
);

  wire and_4_out, and_5_out, and_6_out, and_7_out;

  ROM #(.addrWidth(6), .dataWidth(4), .Select("low")) rom_1 (.addr(in_1[5:0]), .data(out_2));
  and and_1 (out_9, ~in_1[26], ~in_1[27], ~in_1[28], ~in_1[29], ~in_1[30], ~in_1[31]);  // AND_Gate
  and and_2 (out_5, in_1[26], in_1[27], ~in_1[28], ~in_1[29], ~in_1[30], in_1[31]);  // AND_Gate
  and and_3 (out_6, in_1[26], in_1[27], ~in_1[28], in_1[29], ~in_1[30], in_1[31]);  // AND_Gate
  and and_4 (and_4_out, ~in_1[26], ~in_1[27], in_1[28], ~in_1[29], ~in_1[30], ~in_1[31]);  // AND_Gate
  and and_5 (and_5_out, in_1[26], in_1[27], in_1[28], ~in_1[29], ~in_1[30], ~in_1[31]);  // AND_Gate
  and and_6 (and_6_out, in_1[26], ~in_1[27], ~in_1[28], ~in_1[29], ~in_1[30], ~in_1[31]);  // AND_Gate
  and and_7 (and_7_out, in_1[26], ~in_1[27], in_1[28], ~in_1[29], ~in_1[30], ~in_1[31]);  // AND_Gate
  and and_8 (out_4, ~in_1[26], in_1[27], ~in_1[28], ~in_1[29], ~in_1[30], ~in_1[31]);  // AND_Gate
  or or_1 (out_8, and_4_out, and_5_out, and_6_out, and_7_out);
  Multiplexer #(.select(4), .enable("false")) multiplexer_1 (
    .in0(1'b0), .in1(1'b0), .in2(1'b0), .in3(out_5), .in4(1'b0), .in5(1'b0), .in6(1'b0), .in7(1'b0),
    .in8(1'b0), .in9(1'b0), .in10(1'b0), .in11(out_6), .in12(1'b0), .in13(1'b0), .in14(1'b0), .in15(1'b0),
    .out(out_3), .sel(in_1[29:26]));
  Multiplexer #(.select(4), .enable("false")) multiplexer_2 (
    .in0(out_9), .in1(1'b0), .in2(1'b0), .in3(out_5), .in4(1'b0), .in5(1'b0), .in6(1'b0), .in7(1'b0),
    .in8(1'b0), .in9(1'b0), .in10(1'b0), .in11(1'b0), .in12(1'b0), .in13(1'b0), .in14(1'b0), .in15(1'b0),
    .out(out_10), .sel(in_1[29:26]));

  assign out_7 = out_5;

  // Other names for the same wires on the sheet: ALUOp[3:0] = out_2; ALUsrc = out_3; Function[5:0] = in_1[5:0];
  //   Function1[1:0] = in_1[1:0]; Instr[31:0] = in_1; Function2[3:0] = in_1[5:2]; OpCode[5:0] = in_1[31:26];
  //   Jump = out_4; memRead = out_5; memToReg = out_5; memWrite = out_6; PCSrc = out_8; regDst = out_9;
  //   regWrite = out_10

  // Notes on the sheet:
  //   contents of rom_1 (hex, n*v repeats v):
  //   c 33*0 1 0 4 0 0 5 4*0 a
  //   R
  //   LOAD
  //   STORE
  //   BRANCH EQUAL
  //   JUMP
  //   BRANCH GREATER ZERO
  //   BRANCH LESS ZERO
  //   BRANCH NOT EQUAL
endmodule

module Data_Memory (
  input  BMemRead,
  input  [31:0] Address,
  input  BMemWrite,
  input  [31:0] WriteData,
  input  in_5,
  output [31:0] out_6
);

  RAM #(.addrWidth(5), .dataWidth(32), .bus("separate"), .Select("high")) ram_1 (
    .addr(Address[25:21]), .din(WriteData), .data(out_6), .str(BMemWrite), .clk(in_5), .ld(BMemRead));  // open: sel, clr

  // Other names for the same wires on the sheet: Clock = in_5; MemRead = BMemRead; MemWrite = BMemWrite;
  //   ReadData[31:0] = out_6
endmodule
